# Fritzing sketch ATMEGA328P AdaLoader (saved by Fritzing 0.7.12b)
breadboards: 2

parts:
  Arduino1 = Arduino
  U5 = atmega328 [package=dip]
  J1 = Piezo Speaker
  S1 = Pushbutton [package="[THT]"]
  R1 = Resistor [tolerance=±5% resistance=10k package=THT]
  LED1 = LED - 5mm [color="Green (555nm)" package="5 mm [THT]"]
  LED2 = LED - 5mm [color="Red (633nm)" package="5 mm [THT]"]
  R2 = Resistor [tolerance=±5% resistance=220 package=THT]
  R3 = Resistor [tolerance=±5% resistance=220 package=THT]

nets:
  N1: Arduino1.D13, U5.D13
  N2: Arduino1.D12, U5.D12
  N3: Arduino1.D11, U5.D11_(PWM)
  N4: Arduino1.D10, U5.RESET
  N5: Arduino1.D9, U5.XLAT1
  N6: Arduino1.D8, LED2.anode
  +5V: Arduino1.+5V, U5.VCC, U5.AVCC, R1.Pin_1
  GND: Arduino1.GND, U5.GND, J1.pin1, S1.Pin_1, S1.Pin_2
  N7: Arduino1.A0, LED1.anode
  N8: Arduino1.A1, S1.Pin_3, S1.Pin_4, R1.Pin_0
  N9: Arduino1.A3, J1.pin2
  N10: LED1.cathode, R3.Pin_1
  N11: LED2.cathode, R2.Pin_1
  N12: R2.Pin_0, R3.Pin_0
