# Fritzing sketch ATMEGA328P Simple (saved by Fritzing 0.7.12b)
breadboards: 1

parts:
  Part2 = FTDI Basic Programmer
  C8 = Electrolytic Capacitor [capacitance=10µF package="100 mil [THT, electrolytic]"]
  U4 = atmega328 [package=dip]
  XTAL3 = Crystal [frequency="16 Mhz" package=THT]
  C9 = Ceramic Capacitor [capacitance=100nF package="100 mil [THT, multilayer]"]
  C10 = Ceramic Capacitor [capacitance=100nF package="100 mil [THT, multilayer]"]
  C11 = Electrolytic Capacitor [capacitance=10µF package="100 mil [THT, electrolytic]"]
  LED2 = LED - 5mm [color="Red (633nm)" package="5 mm [THT]"]
  R2 = Resistor [tolerance=±5% resistance=220 package=THT]
  LED3 = LED - 5mm [color="Red (633nm)" package="5 mm [THT]"]
  R3 = Resistor [tolerance=±5% resistance=220 package=THT]

nets:
  N1: Part2.DTR, C8.+
  N2: Part2.RXI, U4.D1_(TX)
  N3: Part2.TXO, U4.D0_(RX)
  N4: Part2.POWER, U4.VCC, U4.AVCC, U4.AREF, C11.+, LED2.anode
  GND: Part2.CTS, Part2.GND, U4.GND, C9.1, C10.1, C11.-, R2.Pin_0, R3.Pin_0
  N5: C8.-, U4.RESET
  N6: U4.XLAT1, XTAL3.pin_0, C9.0
  N7: U4.XLAT2, XTAL3.pin_1, C10.0
  N8: U4.D13, LED3.anode
  N9: LED2.cathode, R2.Pin_1
  N10: LED3.cathode, R3.Pin_1
